// Logisim project alu.circ as structural Verilog: 11 circuits, main circuit main
module main (
  input  in_1,
  input  in_2,
  input  [3:0] A,
  input  in_4,
  input  [1:0] S1,
  input  [3:0] B,
  input  in_7,
  input  in_8,
  input  [3:0] in_9,
  input  in_10,
  input  in_11,
  input  in_12,
  input  [1:0] in_13,
  input  in_14,
  input  in_15,
  input  in_16,
  output [3:0] out_17,
  output [3:0] out_18,
  output [3:0] out_19
);

  wire adder_1_cout, comparator_1_eq, comparator_1_gt, comparator_1_lt, decoder3_1_a_2, decoder3_1_b_2,
       decoder3_1_c_2, decoder3_1_d_2, decoder3_1_e, decoder3_1_f, decoder3_1_g;
  wire [3:0] adder_1_out, adder_2_out, and_1_out, multiplexer_1_out, multiplexer_2_out, multiplexer_3_out,
       negator_1_out, not_1_out, or_1_out, subtractor_1_out, xor_1_out;

  assign not_1_out = ~B;  // NOT_Gate not_1, 4 bits wide
  assign and_1_out = B & A;  // AND_Gate and_1, 4 bits wide
  assign or_1_out = A | B;  // OR_Gate or_1, 4 bits wide
  assign xor_1_out = A ^ B;  // XOR_Gate xor_1, 4 bits wide
  Comparator #(.width(4)) comparator_1 (.a(B), .b(A), .gt(comparator_1_gt), .eq(comparator_1_eq), .lt(comparator_1_lt));
  Adder #(.width(4)) adder_1 (.a(A), .b(B), .out(adder_1_out), .cout(adder_1_cout));  // open: cin
  LED led_1 (.in(adder_1_cout));
  Subtractor #(.width(4)) subtractor_1 (.a(A), .b(B), .out(subtractor_1_out));  // open: bin, bout
  Negator #(.width(4)) negator_1 (.in(B), .out(negator_1_out));
  Adder #(.width(4)) adder_2 (.a(A), .b(in_9), .out(adder_2_out));  // open: cin, cout
  LED led_2 (.in(comparator_1_gt));
  LED led_3 (.in(comparator_1_lt));
  Multiplexer #(.select(2), .width(4)) multiplexer_1 (
    .in0(and_1_out), .in1(or_1_out), .in2(xor_1_out), .in3(not_1_out), .out(multiplexer_1_out), .sel(in_13));  // open: en
  LED led_4 (.in(comparator_1_eq));
  Multiplexer #(.select(2), .width(4)) multiplexer_2 (
    .in0(adder_1_out), .in1(subtractor_1_out), .in2(negator_1_out), .in3(adder_2_out),
    .out(multiplexer_2_out), .sel(S1));  // open: en
  Multiplexer #(.width(4)) multiplexer_3 (
    .in0(multiplexer_2_out), .in1(multiplexer_1_out), .out(multiplexer_3_out), .sel(in_11), .en(in_12));
  Register #(.width(4)) register_1 (.D(A), .en(in_1), .Q(out_17), .clk(in_2), .clr(in_4));
  Register #(.width(4)) register_2 (.D(B), .en(in_7), .Q(out_18), .clk(in_8), .clr(in_10));
  decoder3 decoder3_1 (
    .A(multiplexer_3_out[0]), .B(multiplexer_3_out[1]), .C(multiplexer_3_out[2]), .D(multiplexer_3_out[3]),
    .a_2(decoder3_1_a_2), .b_2(decoder3_1_b_2), .c_2(decoder3_1_c_2), .d_2(decoder3_1_d_2), .e(decoder3_1_e),
    .f(decoder3_1_f), .g(decoder3_1_g));
  _7_Segment_Display u_7_segment_display_1 (
    .g(decoder3_1_g), .f(decoder3_1_f), .a(decoder3_1_a_2), .b(decoder3_1_b_2), .e(decoder3_1_e),
    .d(decoder3_1_d_2), .c(decoder3_1_c_2));  // open: dp
  Register #(.width(4)) register_3 (.D(multiplexer_3_out), .en(in_14), .Q(out_19), .clk(in_15), .clr(in_16));
endmodule

module decoder3 (
  input  A,
  input  B,
  input  C,
  input  D,
  output a_2,
  output b_2,
  output c_2,
  output d_2,
  output e,
  output f,
  output g
);

  wire nand_1_out, nand_2_out, nand_3_out, nand_4_out, nand_5_out, nand_6_out, nand_7_out, nand_8_out,
       nand_9_out, nand_10_out, nand_11_out, nand_12_out, nand_13_out, nand_14_out, nand_15_out, nand_16_out,
       nand_17_out, nand_18_out, nand_19_out, nand_20_out, nand_21_out, nand_22_out, nand_23_out,
       nand_24_out, nand_25_out, nand_26_out, nand_27_out, nand_28_out, nand_29_out, nand_30_out,
       nand_31_out, nand_32_out, nand_33_out, nand_34_out, nand_35_out, nand_36_out, nand_37_out,
       nand_38_out, nand_39_out, nand_40_out, nand_41_out, nand_42_out, nand_43_out, nand_44_out,
       nand_45_out, nand_46_out, nand_47_out, nand_48_out, nand_49_out, nand_50_out, nand_51_out,
       nand_52_out, nand_53_out, nand_54_out, nand_55_out, nand_56_out, nand_57_out, nand_58_out,
       nand_59_out, nand_60_out, nand_61_out, nand_62_out, nand_63_out, nand_64_out, nand_65_out,
       nand_66_out, nand_67_out, nand_68_out, nand_69_out, nand_70_out, nand_71_out, nand_72_out,
       nand_73_out, nand_74_out, nand_75_out, nand_76_out, nand_77_out, nand_78_out, nand_79_out,
       nand_80_out, nand_81_out, nand_82_out, nand_83_out, nand_84_out, nand_85_out, nand_86_out,
       nand_87_out, nand_88_out, nand_89_out, nand_90_out, nand_91_out, nand_92_out, nand_93_out,
       nand_94_out, nand_95_out, nand_96_out, nand_97_out, nand_98_out, nand_99_out, nand_100_out,
       nand_101_out, nand_102_out, nand_103_out, nand_104_out, nand_106_out, nand_107_out, nand_108_out,
       nand_109_out, nand_110_out, nand_111_out, nand_112_out, nand_113_out, nand_114_out, nand_115_out,
       nand_116_out, nand_117_out, nand_118_out, nand_119_out, nand_120_out, nand_121_out, nand_122_out,
       nand_123_out, nand_124_out, nand_125_out, nand_126_out, nand_127_out, nand_128_out, nand_129_out,
       nand_130_out, nand_131_out, nand_132_out, nand_133_out, nand_134_out, nand_136_out, nand_137_out,
       nand_138_out, nand_139_out, nand_141_out, nand_142_out, nand_143_out, nand_144_out, nand_145_out,
       nand_146_out, nand_147_out, nand_148_out;

  nand nand_1 (nand_1_out, C, C);
  nand nand_2 (nand_2_out, D, D);
  nand nand_3 (nand_3_out, B, B);
  nand nand_4 (nand_4_out, D, D);
  nand nand_5 (nand_5_out, B, B);
  nand nand_6 (nand_6_out, D, D);
  nand nand_7 (nand_7_out, D, D);
  nand nand_8 (nand_8_out, C, C);
  nand nand_9 (nand_9_out, C, C);
  nand nand_10 (nand_10_out, C, C);
  nand nand_11 (nand_11_out, A, A);
  nand nand_12 (nand_12_out, A, A);
  nand nand_13 (nand_13_out, D, D);
  nand nand_14 (nand_14_out, C, C);
  nand nand_15 (nand_15_out, A, A);
  nand nand_16 (nand_16_out, D, D);
  nand nand_17 (nand_17_out, D, nand_1_out);
  nand nand_18 (nand_18_out, nand_2_out, nand_3_out);
  nand nand_19 (nand_19_out, nand_4_out, nand_5_out);
  nand nand_20 (nand_20_out, nand_6_out, A);
  nand nand_21 (nand_21_out, nand_7_out, nand_8_out);
  nand nand_22 (nand_22_out, nand_9_out, B);
  nand nand_23 (nand_23_out, nand_10_out, nand_11_out);
  nand nand_24 (nand_24_out, B, nand_12_out);
  nand nand_25 (nand_25_out, D, B);
  nand nand_26 (nand_26_out, D, C);
  nand nand_27 (nand_27_out, nand_13_out, C);
  nand nand_28 (nand_28_out, nand_14_out, B);
  nand nand_29 (nand_29_out, B, nand_15_out);
  nand nand_30 (nand_30_out, nand_16_out, C);
  nand nand_31 (nand_31_out, C, C);
  nand nand_32 (nand_32_out, A, A);
  nand nand_33 (nand_33_out, D, D);
  nand nand_34 (nand_34_out, D, D);
  nand nand_35 (nand_35_out, nand_17_out, nand_17_out);
  nand nand_36 (nand_36_out, B, B);
  nand nand_37 (nand_37_out, D, D);
  nand nand_38 (nand_38_out, C, C);
  nand nand_39 (nand_39_out, nand_18_out, nand_18_out);
  nand nand_40 (nand_40_out, A, A);
  nand nand_41 (nand_41_out, D, D);
  nand nand_42 (nand_42_out, B, B);
  nand nand_43 (nand_43_out, nand_19_out, nand_20_out);
  nand nand_44 (nand_44_out, B, B);
  nand nand_45 (nand_45_out, D, D);
  nand nand_46 (nand_46_out, C, C);
  nand nand_47 (nand_47_out, nand_21_out, nand_21_out);
  nand nand_48 (nand_48_out, A, A);
  nand nand_49 (nand_49_out, nand_22_out, nand_22_out);
  nand nand_50 (nand_50_out, B, B);
  nand nand_51 (nand_51_out, B, B);
  nand nand_52 (nand_52_out, nand_23_out, nand_24_out);
  nand nand_53 (nand_53_out, nand_25_out, nand_26_out);
  nand nand_54 (nand_54_out, B, B);
  nand nand_55 (nand_55_out, A, A);
  nand nand_56 (nand_56_out, nand_27_out, nand_27_out);
  nand nand_57 (nand_57_out, B, B);
  nand nand_58 (nand_58_out, nand_28_out, nand_29_out);
  nand nand_59 (nand_59_out, nand_30_out, nand_30_out);
  nand nand_60 (nand_60_out, B, B);
  nand nand_61 (nand_61_out, C, C);
  nand nand_62 (nand_62_out, nand_31_out, nand_32_out);
  nand nand_63 (nand_63_out, nand_33_out, B);
  nand nand_64 (nand_64_out, nand_34_out, C);
  nand nand_65 (nand_65_out, C, B);
  nand nand_66 (nand_66_out, nand_35_out, nand_36_out);
  nand nand_67 (nand_67_out, nand_37_out, nand_38_out);
  nand nand_68 (nand_68_out, nand_39_out, nand_40_out);
  nand nand_69 (nand_69_out, nand_41_out, B);
  nand nand_70 (nand_70_out, D, nand_42_out);
  nand nand_71 (nand_71_out, nand_43_out, nand_43_out);
  nand nand_72 (nand_72_out, nand_44_out, A);
  nand nand_73 (nand_73_out, nand_45_out, C);
  nand nand_74 (nand_74_out, D, nand_46_out);
  nand nand_75 (nand_75_out, nand_47_out, nand_48_out);
  nand nand_76 (nand_76_out, nand_49_out, A);
  nand nand_77 (nand_77_out, C, nand_50_out);
  nand nand_78 (nand_78_out, C, B);
  nand nand_79 (nand_79_out, D, nand_51_out);
  nand nand_80 (nand_80_out, nand_52_out, nand_52_out);
  nand nand_81 (nand_81_out, nand_53_out, nand_53_out);
  nand nand_82 (nand_82_out, nand_54_out, nand_55_out);
  nand nand_83 (nand_83_out, nand_56_out, nand_57_out);
  nand nand_84 (nand_84_out, nand_58_out, nand_58_out);
  nand nand_85 (nand_85_out, nand_59_out, nand_60_out);
  nand nand_86 (nand_86_out, D, nand_61_out);
  nand nand_87 (nand_87_out, D, A);
  nand nand_88 (nand_88_out, nand_62_out, nand_63_out);
  nand nand_89 (nand_89_out, nand_64_out, nand_64_out);
  nand nand_90 (nand_90_out, nand_65_out, nand_66_out);
  nand nand_91 (nand_91_out, A, A);
  nand nand_92 (nand_92_out, nand_67_out, nand_68_out);
  nand nand_93 (nand_93_out, C, C);
  nand nand_94 (nand_94_out, A, A);
  nand nand_95 (nand_95_out, nand_69_out, nand_69_out);
  nand nand_96 (nand_96_out, nand_70_out, nand_70_out);
  nand nand_97 (nand_97_out, nand_71_out, nand_72_out);
  nand nand_98 (nand_98_out, nand_73_out, nand_74_out);
  nand nand_99 (nand_99_out, nand_75_out, nand_76_out);
  nand nand_100 (nand_100_out, nand_77_out, nand_77_out);
  nand nand_101 (nand_101_out, nand_78_out, nand_78_out);
  nand nand_102 (nand_102_out, A, A);
  nand nand_103 (nand_103_out, nand_79_out, nand_79_out);
  nand nand_104 (nand_104_out, A, A);
  nand nand_105 (e, nand_80_out, nand_81_out);
  nand nand_106 (nand_106_out, nand_82_out, nand_83_out);
  nand nand_107 (nand_107_out, A, A);
  nand nand_108 (nand_108_out, C, C);
  nand nand_109 (nand_109_out, nand_84_out, nand_85_out);
  nand nand_110 (nand_110_out, nand_86_out, nand_87_out);
  nand nand_111 (nand_111_out, nand_88_out, nand_88_out);
  nand nand_112 (nand_112_out, nand_89_out, A);
  nand nand_113 (nand_113_out, nand_90_out, nand_90_out);
  nand nand_114 (nand_114_out, D, nand_91_out);
  nand nand_115 (nand_115_out, nand_92_out, nand_92_out);
  nand nand_116 (nand_116_out, nand_93_out, nand_94_out);
  nand nand_117 (nand_117_out, nand_95_out, A);
  nand nand_118 (nand_118_out, nand_96_out, A);
  nand nand_119 (nand_119_out, nand_97_out, nand_97_out);
  nand nand_120 (nand_120_out, nand_98_out, nand_98_out);
  nand nand_121 (nand_121_out, nand_99_out, nand_99_out);
  nand nand_122 (nand_122_out, nand_100_out, A);
  nand nand_123 (nand_123_out, nand_101_out, nand_102_out);
  nand nand_124 (nand_124_out, nand_103_out, nand_104_out);
  nand nand_125 (nand_125_out, nand_106_out, nand_106_out);
  nand nand_126 (nand_126_out, C, nand_107_out);
  nand nand_127 (nand_127_out, D, nand_108_out);
  nand nand_128 (nand_128_out, D, B);
  nand nand_129 (nand_129_out, nand_109_out, nand_109_out);
  nand nand_130 (nand_130_out, nand_110_out, nand_110_out);
  nand nand_131 (nand_131_out, nand_111_out, nand_112_out);
  nand nand_132 (nand_132_out, nand_113_out, nand_114_out);
  nand nand_133 (nand_133_out, nand_115_out, nand_116_out);
  nand nand_134 (nand_134_out, nand_117_out, nand_118_out);
  nand nand_135 (c_2, nand_119_out, nand_120_out);
  nand nand_136 (nand_136_out, nand_121_out, nand_122_out);
  nand nand_137 (nand_137_out, nand_123_out, nand_124_out);
  nand nand_138 (nand_138_out, nand_125_out, nand_126_out);
  nand nand_139 (nand_139_out, nand_127_out, nand_128_out);
  nand nand_140 (g, nand_129_out, nand_130_out);
  nand nand_141 (nand_141_out, nand_131_out, nand_131_out);
  nand nand_142 (nand_142_out, nand_132_out, nand_132_out);
  nand nand_143 (nand_143_out, nand_133_out, nand_133_out);
  nand nand_144 (nand_144_out, nand_134_out, nand_134_out);
  nand nand_145 (nand_145_out, nand_136_out, nand_136_out);
  nand nand_146 (nand_146_out, nand_137_out, nand_137_out);
  nand nand_147 (nand_147_out, nand_138_out, nand_138_out);
  nand nand_148 (nand_148_out, nand_139_out, nand_139_out);
  nand nand_149 (a_2, nand_141_out, nand_142_out);
  nand nand_150 (b_2, nand_143_out, nand_144_out);
  nand nand_151 (d_2, nand_145_out, nand_146_out);
  nand nand_152 (f, nand_147_out, nand_148_out);
endmodule

module fulladder (
  input  B,
  input  A,
  input  Cin
);

  wire and_1_out, and_2_out, or_1_out, xor_1_out, xor_2_out;

  xor xor_1 (xor_1_out, A, B);
  xor xor_2 (xor_2_out, xor_1_out, Cin);
  and and_1 (and_1_out, xor_1_out, Cin);
  and and_2 (and_2_out, A, B);
  LED led_1 (.in(xor_2_out));
  LED led_2 (.in(or_1_out));
  or or_1 (or_1_out, and_1_out, and_2_out);
endmodule

module _4bit_fulladder (
  input  A0,
  input  B0,
  input  A1,
  input  B1,
  input  A2,
  input  B2,
  input  A3,
  input  B3,
  output R0,
  output R1,
  output R2,
  output R3,
  output C
);

  wire fulladder1_1_s, fulladder1_2_s, fulladder1_3_s;

  fulladder1 fulladder1_1 (.x1(1'b0), .x0(A0), .ci(B0), .co(R0), .s(fulladder1_1_s));
  fulladder1 fulladder1_2 (.x1(fulladder1_1_s), .x0(A1), .ci(B1), .co(R1), .s(fulladder1_2_s));
  fulladder1 fulladder1_3 (.x1(fulladder1_2_s), .x0(A2), .ci(B2), .co(R2), .s(fulladder1_3_s));
  fulladder1 fulladder1_4 (.x1(fulladder1_3_s), .x0(A3), .ci(B3), .co(R3), .s(C));
endmodule

module _4bit_subtractor (
  input  in_1,
  input  in_2,
  input  in_3,
  input  in_4,
  input  in_5,
  input  in_6,
  input  in_7,
  input  in_8,
  output out_9,
  output out_10,
  output out_11,
  output out_12,
  output out_13
);

  wire fullsubtractor_1_out_5, fullsubtractor_2_out_5, fullsubtractor_3_out_5;

  fullsubtractor fullsubtractor_1 (
    .in_1(in_1), .in_2(in_2), .in_3(1'b0), .out_4(out_9), .out_5(fullsubtractor_1_out_5));
  fullsubtractor fullsubtractor_2 (
    .in_1(in_3), .in_2(in_4), .in_3(fullsubtractor_1_out_5), .out_4(out_10), .out_5(fullsubtractor_2_out_5));
  fullsubtractor fullsubtractor_3 (
    .in_1(in_5), .in_2(in_6), .in_3(fullsubtractor_2_out_5), .out_4(out_11), .out_5(fullsubtractor_3_out_5));
  fullsubtractor fullsubtractor_4 (
    .in_1(in_7), .in_2(in_8), .in_3(fullsubtractor_3_out_5), .out_4(out_12), .out_5(out_13));
endmodule

module _4_bit_register (
  input  [3:0] in_1,
  input  in_2,
  input  in_3,
  input  in_4,
  output [3:0] out_5
);

  Register #(.width(4)) register_1 (.D(in_1), .en(in_2), .Q(out_5), .clk(in_3), .clr(in_4));
endmodule

module halfadder (
  input  in_1,
  input  in_2,
  output out_3,
  output out_4
);

  and and_1 (out_3, in_1, in_2);
  xor xor_1 (out_4, in_1, in_2);
endmodule

module fulladder1 (
  input  x1,
  input  x0,
  input  ci,
  output co,
  output s
);

  wire halfadder_1_out_3, halfadder_1_out_4, halfadder_2_out_3;

  halfadder halfadder_1 (.in_1(x1), .in_2(x0), .out_3(halfadder_1_out_3), .out_4(halfadder_1_out_4));
  halfadder halfadder_2 (.in_1(halfadder_1_out_4), .in_2(ci), .out_3(halfadder_2_out_3), .out_4(s));
  or or_1 (co, halfadder_1_out_3, halfadder_2_out_3);
endmodule

module _8_1_mux (
  input  [3:0] in_1,
  input  [3:0] in_2,
  input  [3:0] in_3,
  input  [3:0] in_4,
  input  [3:0] in_5,
  input  [3:0] in_6,
  input  [3:0] in_7,
  input  [3:0] in_8,
  input  [2:0] in_9,
  output [3:0] out_10,
  output out_11,
  output out_12,
  output out_13,
  output out_14
);

  Multiplexer #(.select(3), .width(4), .disabled(0), .enable("false")) multiplexer_1 (
    .in0(in_1), .in1(in_2), .in2(in_3), .in3(in_4), .in4(in_5), .in5(in_6), .in6(in_7), .in7(in_8),
    .out(out_10), .sel(in_9));

  assign out_11 = out_10[0];
  assign out_12 = out_10[1];
  assign out_13 = out_10[2];
  assign out_14 = out_10[3];
endmodule

module halfsubtractor (
  input  in_1,
  input  in_2,
  output out_3,
  output out_4
);

  and and_1 (out_4, ~in_1, in_2);  // AND_Gate
  xor xor_1 (out_3, in_1, in_2);
endmodule

module fullsubtractor (
  input  in_1,
  input  in_2,
  input  in_3,
  output out_4,
  output out_5
);

  wire halfsubtractor_1_out_3, halfsubtractor_1_out_4, halfsubtractor_2_out_4;

  halfsubtractor halfsubtractor_1 (
    .in_1(in_1), .in_2(in_2), .out_3(halfsubtractor_1_out_3), .out_4(halfsubtractor_1_out_4));
  halfsubtractor halfsubtractor_2 (
    .in_1(halfsubtractor_1_out_3), .in_2(in_3), .out_3(out_4), .out_4(halfsubtractor_2_out_4));
  or or_1 (out_5, halfsubtractor_2_out_4, halfsubtractor_1_out_4);
endmodule
